# Fritzing sketch Hugin_PCB (saved by Fritzing 0.8.7b)
breadboards: 1

parts:
  U1 = mystery part, 8 pins [chip_label=FreeIMUv04]
  Part1 = Logic Level Converter
  Q1 = NPN-Transistor [package="TO92 [THT]"]
  J1 = female pin header, 3 pins [form="♀ (female)"]
  R1 = Resistor [tolerance=±5% resistance=1.2k package=THT]
  R2 = Resistor [tolerance=±5% resistance=2.2k package=THT]
  J2 = female pin header, 4 pins [form="♀ (female)"]
  BeagleBone1 = BeagleBone Black
  U2 = atmega328 [package=dip]
  XTAL1 = Crystal [frequency="16 Mhz" package=THT]
  C1 = Ceramic Capacitor [capacitance=100nF package="100 mil [THT, multilayer]"]
  C2 = Ceramic Capacitor [capacitance=100nF package="100 mil [THT, multilayer]"]
  J3 = female pin header, 4 pins [form="♀ (female)"]
  J4 = female pin header, 4 pins [form="♀ (female)"]
  J5 = female pin header, 4 pins [form="♀ (female)"]
  J6 = female pin header, 4 pins [form="♀ (female)"]
  J7 = female pin header, 4 pins [form="♀ (female)"]

nets:
  N1: U1.pin4, BeagleBone1.no_name_yet#19, U2.A5
  N2: U1.pin5, BeagleBone1.no_name_yet#20, U2.A4
  N3: U1.pin6, Part1.LV, BeagleBone1.no_name_yet#4
  N4: U1.pin8, Q1.E, U2.GND#7
  N5: Part1.GND, J1.pin3, BeagleBone1.no_name_yet#2, U2.GND#21, C1.1, C2.1, J4.pin1, J4.pin2, J4.pin3, J4.pin4, J5.pin1, J5.pin2, J5.pin3, J5.pin4
  N6: Part1.TX_LV, J1.pin1
  N7: Part1.TX_HV, R1.Pin_0
  N8: Part1.HV, J1.pin2, R2.Pin_0, BeagleBone1.no_name_yet#6, U2.VCC, U2.AVCC
  N9: Q1.B, R1.Pin_1
  N10: Q1.C, R2.Pin_1, U2.D0_(RX)
  N11: J2.pin1, U2.D2
  N12: J2.pin2, U2.D3_(PWM)
  N13: J2.pin3, U2.D4
  N14: J2.pin4, U2.D5_(PWM)
  N15: U2.XLAT1, XTAL1.pin_0, C2.0
  N16: U2.XLAT2, XTAL1.pin_1, C1.0
  N17: U2.D6_(PWM), J7.pin1
  N18: U2.D9_(PWM), J7.pin2
  N19: U2.D10_(PWM), J7.pin3
  N20: U2.D11_(PWM), J7.pin4
  N21: J3.pin1, J3.pin2, J3.pin3, J3.pin4
  N22: J6.pin1, J6.pin2, J6.pin3, J6.pin4

notes:
  Inverter
  Third line is 5V from barrel plug. Fourth line is internal 5V
  COTS-läsning
  PWM UT
  S.Bus

custom parts:
  BeagleBone Black: BeagleBone Black rev. A5B
